# Fritzing sketch Untitled Sketch (saved by Fritzing 0.9.3b)
breadboards: 1

parts:
  Part1 = Arduino Nano (Rev3.0) (ICSP)
  RHT1 = Humidity and Temperature Sensor RHT03
  R1 = Resistor [tolerance=±5% resistance=1k package="2512 [SMD]"]  # not connected
  U1 = WS2812 RGB LED strip

nets:
  N1: Part1.D3, U1.DIN
  N2: Part1.D5, RHT1.Data-signal
  GND: Part1.GND, RHT1.GND_2, U1.GND
  VCC: Part1.5V, RHT1.Vcc, U1.VCC

custom parts:
  WS2812 RGB LED strip: WS2812 strip
